// Digital circuit 16-BitAndOP.dig as structural Verilog
module _16_BitAndOP (
  input  [15:0] A,
  input  [15:0] B,
  output [15:0] Q
);

  and and_1 (Q[0], A[0], B[0]);
  and and_2 (Q[1], A[1], B[1]);
  and and_3 (Q[2], A[2], B[2]);
  and and_4 (Q[3], A[3], B[3]);
  and and_5 (Q[4], A[4], B[4]);
  and and_6 (Q[5], A[5], B[5]);
  and and_7 (Q[6], A[6], B[6]);
  and and_8 (Q[7], A[7], B[7]);
  and and_9 (Q[8], A[8], B[8]);
  and and_10 (Q[9], A[9], B[9]);
  and and_11 (Q[10], A[10], B[10]);
  and and_12 (Q[11], A[11], B[11]);
  and and_13 (Q[12], A[12], B[12]);
  and and_14 (Q[13], A[13], B[13]);
  and and_15 (Q[14], A[14], B[14]);
  and and_16 (Q[15], A[15], B[15]);
endmodule
