// Digital circuit 16-BitDecoderWithEnablePin.dig as structural Verilog
module _16_BitDecoderWithEnablePin (
  input  EN,
  input  [3:0] Sel_4Bit,
  output Q0,
  output Q1,
  output Q2,
  output Q3,
  output Q4,
  output Q5,
  output Q6,
  output Q7,
  output Q8,
  output Q9,
  output Q10,
  output Q11,
  output Q12,
  output Q13,
  output Q14,
  output Q15
);

  wire decoder_1_out_0, decoder_1_out_1, decoder_1_out_2, decoder_1_out_3, decoder_1_out_4, decoder_1_out_5,
       decoder_1_out_6, decoder_1_out_7, decoder_1_out_8, decoder_1_out_9, decoder_1_out_10,
       decoder_1_out_11, decoder_1_out_12, decoder_1_out_13, decoder_1_out_14, decoder_1_out_15;

  Decoder #(.Selector_Bits(4)) decoder_1 (
    .sel(Sel_4Bit), .out_0(decoder_1_out_0), .out_1(decoder_1_out_1), .out_2(decoder_1_out_2),
    .out_3(decoder_1_out_3), .out_4(decoder_1_out_4), .out_5(decoder_1_out_5), .out_6(decoder_1_out_6),
    .out_7(decoder_1_out_7), .out_8(decoder_1_out_8), .out_9(decoder_1_out_9), .out_10(decoder_1_out_10),
    .out_11(decoder_1_out_11), .out_12(decoder_1_out_12), .out_13(decoder_1_out_13),
    .out_14(decoder_1_out_14), .out_15(decoder_1_out_15));
  and and_1 (Q0, EN, decoder_1_out_0);
  and and_2 (Q1, EN, decoder_1_out_1);
  and and_3 (Q2, EN, decoder_1_out_2);
  and and_4 (Q3, EN, decoder_1_out_3);
  and and_5 (Q4, EN, decoder_1_out_4);
  and and_6 (Q5, EN, decoder_1_out_5);
  and and_7 (Q6, EN, decoder_1_out_6);
  and and_8 (Q7, EN, decoder_1_out_7);
  and and_9 (Q8, EN, decoder_1_out_8);
  and and_10 (Q9, EN, decoder_1_out_9);
  and and_11 (Q10, EN, decoder_1_out_10);
  and and_12 (Q11, EN, decoder_1_out_11);
  and and_13 (Q12, EN, decoder_1_out_12);
  and and_14 (Q13, EN, decoder_1_out_13);
  and and_15 (Q14, EN, decoder_1_out_14);
  and and_16 (Q15, EN, decoder_1_out_15);
endmodule
