// Digital circuit 16-BitNotOP.dig as structural Verilog
module _16_BitNotOP (
  input  [15:0] D,
  output [15:0] Q
);

  not not_1 (Q[0], D[0]);
  not not_2 (Q[1], D[1]);
  not not_3 (Q[2], D[2]);
  not not_4 (Q[3], D[3]);
  not not_5 (Q[4], D[4]);
  not not_6 (Q[5], D[5]);
  not not_7 (Q[6], D[6]);
  not not_8 (Q[7], D[7]);
  not not_9 (Q[8], D[8]);
  not not_10 (Q[9], D[9]);
  not not_11 (Q[10], D[10]);
  not not_12 (Q[11], D[11]);
  not not_13 (Q[12], D[12]);
  not not_14 (Q[13], D[13]);
  not not_15 (Q[14], D[14]);
  not not_16 (Q[15], D[15]);
endmodule
