// Digital circuit 16-BitOrOP.dig as structural Verilog
module _16_BitOrOP (
  input  [15:0] A,
  input  [15:0] B,
  output [15:0] Q
);

  or or_1 (Q[0], A[0], B[0]);
  or or_2 (Q[1], A[1], B[1]);
  or or_3 (Q[2], A[2], B[2]);
  or or_4 (Q[3], A[3], B[3]);
  or or_5 (Q[4], A[4], B[4]);
  or or_6 (Q[5], A[5], B[5]);
  or or_7 (Q[6], A[6], B[6]);
  or or_8 (Q[7], A[7], B[7]);
  or or_9 (Q[8], A[8], B[8]);
  or or_10 (Q[9], A[9], B[9]);
  or or_11 (Q[10], A[10], B[10]);
  or or_12 (Q[11], A[11], B[11]);
  or or_13 (Q[12], A[12], B[12]);
  or or_14 (Q[13], A[13], B[13]);
  or or_15 (Q[14], A[14], B[14]);
  or or_16 (Q[15], A[15], B[15]);
endmodule
