// Digital circuit 16-BitRegister.dig as structural Verilog
module _16_BitRegister (
  input  [15:0] D,
  input  EN,
  input  CLK,
  output Q0,
  output Q1,
  output Q2,
  output Q3,
  output Q4,
  output Q5,
  output Q6,
  output Q7,
  output Q8,
  output Q9,
  output Q10,
  output Q11,
  output Q12,
  output Q13,
  output Q14,
  output Q15
);

  Register reg1 (.D(D[0]), .C(CLK), .en(EN), .Q(Q0));
  Register reg2 (.D(D[1]), .C(CLK), .en(EN), .Q(Q1));
  Register reg3 (.D(D[2]), .C(CLK), .en(EN), .Q(Q2));
  Register reg4 (.D(D[3]), .C(CLK), .en(EN), .Q(Q3));
  Register reg5 (.D(D[4]), .C(CLK), .en(EN), .Q(Q4));
  Register reg6 (.D(D[5]), .C(CLK), .en(EN), .Q(Q5));
  Register reg7 (.D(D[6]), .C(CLK), .en(EN), .Q(Q6));
  Register reg8 (.D(D[7]), .C(CLK), .en(EN), .Q(Q7));
  Register reg9 (.D(D[8]), .C(CLK), .en(EN), .Q(Q8));
  Register reg10 (.D(D[9]), .C(CLK), .en(EN), .Q(Q9));
  Register reg11 (.D(D[10]), .C(CLK), .en(EN), .Q(Q10));
  Register reg12 (.D(D[11]), .C(CLK), .en(EN), .Q(Q11));
  Register reg13 (.D(D[12]), .C(CLK), .en(EN), .Q(Q12));
  Register reg14 (.D(D[13]), .C(CLK), .en(EN), .Q(Q13));
  Register reg15 (.D(D[14]), .C(CLK), .en(EN), .Q(Q14));
  Register reg16 (.D(D[15]), .C(CLK), .en(EN), .Q(Q15));
  // Pins of 1 and 16 bits meet at D
endmodule
