// Digital circuit 16-BitXorOP.dig as structural Verilog
module _16_BitXorOP (
  input  [15:0] A,
  input  [15:0] B,
  output [15:0] Q
);

  xor xor_1 (Q[0], A[0], B[0]);
  xor xor_2 (Q[1], A[1], B[1]);
  xor xor_3 (Q[2], A[2], B[2]);
  xor xor_4 (Q[3], A[3], B[3]);
  xor xor_5 (Q[4], A[4], B[4]);
  xor xor_6 (Q[5], A[5], B[5]);
  xor xor_7 (Q[6], A[6], B[6]);
  xor xor_8 (Q[7], A[7], B[7]);
  xor xor_9 (Q[8], A[8], B[8]);
  xor xor_10 (Q[9], A[9], B[9]);
  xor xor_11 (Q[10], A[10], B[10]);
  xor xor_12 (Q[11], A[11], B[11]);
  xor xor_13 (Q[12], A[12], B[12]);
  xor xor_14 (Q[13], A[13], B[13]);
  xor xor_15 (Q[14], A[14], B[14]);
  xor xor_16 (Q[15], A[15], B[15]);
endmodule
