// Digital circuit 256bits-regRst.dig as structural Verilog
module _256bits_regRst (
  input  [63:0] D0,
  input  [63:0] D1,
  input  [63:0] D2,
  input  [63:0] D3,
  input  RST,
  output [15:0] Q0,
  output [15:0] Q1,
  output [15:0] Q2,
  output [15:0] Q3,
  output [15:0] Q4,
  output [15:0] Q5,
  output [15:0] Q6,
  output [15:0] Q7,
  output [15:0] Q8,
  output [15:0] Q9,
  output [15:0] Q10,
  output [15:0] Q11,
  output [15:0] Q12,
  output [15:0] Q13,
  output [15:0] Q14,
  output [15:0] Q15
);

  ALU_RegRST alu_regrst_1 (.D(D0[15:0]), .RST(RST), .Q(Q0));
  ALU_RegRST alu_regrst_2 (.D(D0[31:16]), .RST(RST), .Q(Q1));
  ALU_RegRST alu_regrst_3 (.D(D0[47:32]), .RST(RST), .Q(Q2));
  ALU_RegRST alu_regrst_4 (.D(D0[63:48]), .RST(RST), .Q(Q3));
  ALU_RegRST alu_regrst_5 (.D(D1[15:0]), .RST(RST), .Q(Q4));
  ALU_RegRST alu_regrst_6 (.D(D1[31:16]), .RST(RST), .Q(Q5));
  ALU_RegRST alu_regrst_7 (.D(D1[47:32]), .RST(RST), .Q(Q6));
  ALU_RegRST alu_regrst_8 (.D(D1[63:48]), .RST(RST), .Q(Q7));
  ALU_RegRST alu_regrst_9 (.D(D2[15:0]), .RST(RST), .Q(Q8));
  ALU_RegRST alu_regrst_10 (.D(D2[31:16]), .RST(RST), .Q(Q9));
  ALU_RegRST alu_regrst_11 (.D(D2[47:32]), .RST(RST), .Q(Q10));
  ALU_RegRST alu_regrst_12 (.D(D2[63:48]), .RST(RST), .Q(Q11));
  ALU_RegRST alu_regrst_13 (.D(D3[15:0]), .RST(RST), .Q(Q12));
  ALU_RegRST alu_regrst_14 (.D(D3[31:16]), .RST(RST), .Q(Q13));
  ALU_RegRST alu_regrst_15 (.D(D3[47:32]), .RST(RST), .Q(Q14));
  ALU_RegRST alu_regrst_16 (.D(D3[63:48]), .RST(RST), .Q(Q15));
endmodule
