// Digital circuit ALU-RegCtrl.dig as structural Verilog
module ALU_RegCtrl (
  input  IsEn__Decoder,
  input  CLK,
  input  _0x0,
  input  _0x1,
  input  _0x2,
  input  _0x3,
  input  _0x4,
  input  _0x5,
  input  _0x6,
  input  _0x7,
  input  _0x8,
  input  _0x9,
  input  _0xA,
  input  _0xB,
  input  _0xC,
  input  _0xD,
  input  _0xE,
  input  _0xF,
  input  [3:0] OPCODE_IN,
  output Q_0,
  output Q_1,
  output Q_2,
  output Q_3,
  output Q_4,
  output Q_5,
  output Q_6,
  output Q_7,
  output Q_8,
  output Q_9,
  output Q_A,
  output Q_B,
  output Q_C,
  output Q_D,
  output Q_E,
  output Q_F,
  output RST,
  output [3:0] OPCODE_OUT
);

  wire d_ff_1_q, d_ff_2_q, d_ff_3_q, d_ff_4_q, d_ff_5_q, d_ff_6_q, d_ff_7_q, d_ff_8_q, d_ff_9_q, d_ff_10_q,
       d_ff_11_q, d_ff_12_q, d_ff_13_q, d_ff_14_q, d_ff_15_q, d_ff_16_q;

  not not_1 (RST, IsEn__Decoder);
  D_FF d_ff_1 (.D(_0x0), .C(CLK), .Q(d_ff_1_q));  // open: nQ
  D_FF d_ff_2 (.D(_0x1), .C(CLK), .Q(d_ff_2_q));  // open: nQ
  D_FF d_ff_3 (.D(_0x2), .C(CLK), .Q(d_ff_3_q));  // open: nQ
  D_FF d_ff_4 (.D(_0x3), .C(CLK), .Q(d_ff_4_q));  // open: nQ
  D_FF d_ff_5 (.D(_0x4), .C(CLK), .Q(d_ff_5_q));  // open: nQ
  D_FF d_ff_6 (.D(_0x5), .C(CLK), .Q(d_ff_6_q));  // open: nQ
  D_FF d_ff_7 (.D(_0x6), .C(CLK), .Q(d_ff_7_q));  // open: nQ
  D_FF d_ff_8 (.D(_0x7), .C(CLK), .Q(d_ff_8_q));  // open: nQ
  D_FF d_ff_9 (.D(_0x8), .C(CLK), .Q(d_ff_9_q));  // open: nQ
  D_FF d_ff_10 (.D(_0x9), .C(CLK), .Q(d_ff_10_q));  // open: nQ
  D_FF d_ff_11 (.D(_0xA), .C(CLK), .Q(d_ff_11_q));  // open: nQ
  D_FF d_ff_12 (.D(_0xB), .C(CLK), .Q(d_ff_12_q));  // open: nQ
  D_FF d_ff_13 (.D(_0xC), .C(CLK), .Q(d_ff_13_q));  // open: nQ
  D_FF d_ff_14 (.D(_0xD), .C(CLK), .Q(d_ff_14_q));  // open: nQ
  D_FF d_ff_15 (.D(_0xE), .C(CLK), .Q(d_ff_15_q));  // open: nQ
  D_FF d_ff_16 (.D(_0xF), .C(CLK), .Q(d_ff_16_q));  // open: nQ
  D_FF #(.Bits(4)) d_ff_17 (.D(OPCODE_IN), .C(CLK), .Q(OPCODE_OUT));  // open: nQ
  or or_1 (Q_0, RST, d_ff_1_q);
  or or_2 (Q_1, RST, d_ff_2_q);
  or or_3 (Q_2, RST, d_ff_3_q);
  or or_4 (Q_3, RST, d_ff_4_q);
  or or_5 (Q_4, RST, d_ff_5_q);
  or or_6 (Q_5, RST, d_ff_6_q);
  or or_7 (Q_6, RST, d_ff_7_q);
  or or_8 (Q_7, RST, d_ff_8_q);
  or or_9 (Q_8, RST, d_ff_9_q);
  or or_10 (Q_9, RST, d_ff_10_q);
  or or_11 (Q_A, RST, d_ff_11_q);
  or or_12 (Q_B, RST, d_ff_12_q);
  or or_13 (Q_C, RST, d_ff_13_q);
  or or_14 (Q_D, RST, d_ff_14_q);
  or or_15 (Q_E, RST, d_ff_15_q);
  or or_16 (Q_F, RST, d_ff_16_q);
endmodule
