// Digital circuit ALU-RegRST.dig as structural Verilog
module ALU_RegRST (
  input  [15:0] D,
  input  RST,
  output [15:0] Q
);

  wire not_1_out;

  not not_1 (not_1_out, RST);
  and and_1 (Q[0], not_1_out, D[0]);
  and and_2 (Q[1], not_1_out, D[1]);
  and and_3 (Q[2], not_1_out, D[2]);
  and and_4 (Q[3], not_1_out, D[3]);
  and and_5 (Q[4], not_1_out, D[4]);
  and and_6 (Q[5], not_1_out, D[5]);
  and and_7 (Q[6], not_1_out, D[6]);
  and and_8 (Q[7], not_1_out, D[7]);
  and and_9 (Q[8], not_1_out, D[8]);
  and and_10 (Q[9], not_1_out, D[9]);
  and and_11 (Q[10], not_1_out, D[10]);
  and and_12 (Q[11], not_1_out, D[11]);
  and and_13 (Q[12], not_1_out, D[12]);
  and and_14 (Q[13], not_1_out, D[13]);
  and and_15 (Q[14], not_1_out, D[14]);
  and and_16 (Q[15], not_1_out, D[15]);
endmodule
