// Digital circuit Barrel_Shifter.dig as structural Verilog
module Barrel_Shifter (
  input  [15:0] DATA_IN,
  input  [3:0] SHIFT_AMT,
  input  IsLeft,
  input  ARIGHT_LOGIC,
  input  IsRotate,
  output [15:0] DATA_OUT
);

  wire and_1_out;
  wire [1:0] multiplexer_4_out;
  wire [3:0] multiplexer_5_out;
  wire [7:0] multiplexer_6_out;
  wire [15:0] multiplexer_2_out;
  wire [23:0] multiplexer_6_out_2;
  wire [27:0] multiplexer_5_out_2;
  wire [29:0] multiplexer_4_out_2;
  wire [31:0] multiplexer_3_out, multiplexer_7_out;
  wire [31:16] multiplexer_1_out;

  Multiplexer #(.Bits(16)) multiplexer_1 (
    .sel(IsLeft), .in_0(DATA_IN),
    .in_1({DATA_IN[0], DATA_IN[1], DATA_IN[2], DATA_IN[3], DATA_IN[4], DATA_IN[5], DATA_IN[6], DATA_IN[7], DATA_IN[8], DATA_IN[9], DATA_IN[10], DATA_IN[11], DATA_IN[12], DATA_IN[13], DATA_IN[14], DATA_IN[15]}),
    .out(multiplexer_1_out));
  Multiplexer #(.Bits(16)) multiplexer_2 (
    .sel(and_1_out), .in_0({16{1'b0}}), .in_1({16{1'b1}}), .out(multiplexer_2_out));
  and and_1 (and_1_out, DATA_IN[15], ARIGHT_LOGIC);
  Multiplexer #(.Bits(32)) multiplexer_3 (
    .sel(IsRotate), .in_0({multiplexer_2_out, multiplexer_1_out}),
    .in_1({multiplexer_1_out, multiplexer_1_out}), .out(multiplexer_3_out));
  Multiplexer #(.Bits(32)) multiplexer_4 (
    .sel(SHIFT_AMT[0]), .in_0(multiplexer_3_out), .in_1({1'b0, multiplexer_3_out[31:1]}),
    .out({multiplexer_4_out_2, multiplexer_4_out}));
  Multiplexer #(.Bits(32)) multiplexer_5 (
    .sel(SHIFT_AMT[1]), .in_0({multiplexer_4_out_2, multiplexer_4_out}), .in_1({2'b00, multiplexer_4_out_2}),
    .out({multiplexer_5_out_2, multiplexer_5_out}));
  Multiplexer #(.Bits(32)) multiplexer_6 (
    .sel(SHIFT_AMT[2]), .in_0({multiplexer_5_out_2, multiplexer_5_out}),
    .in_1({4'b0000, multiplexer_5_out_2}), .out({multiplexer_6_out_2, multiplexer_6_out}));
  Multiplexer #(.Bits(32)) multiplexer_7 (
    .sel(SHIFT_AMT[3]), .in_0({multiplexer_6_out_2, multiplexer_6_out}),
    .in_1({{8{1'b0}}, multiplexer_6_out_2}), .out(multiplexer_7_out));
  Multiplexer #(.Bits(16)) multiplexer_8 (
    .sel(IsLeft), .in_0(multiplexer_7_out[15:0]),
    .in_1({multiplexer_7_out[0], multiplexer_7_out[1], multiplexer_7_out[2], multiplexer_7_out[3], multiplexer_7_out[4], multiplexer_7_out[5], multiplexer_7_out[6], multiplexer_7_out[7], multiplexer_7_out[8], multiplexer_7_out[9], multiplexer_7_out[10], multiplexer_7_out[11], multiplexer_7_out[12], multiplexer_7_out[13], multiplexer_7_out[14], multiplexer_7_out[15]}),
    .out(DATA_OUT));
endmodule
