// Digital circuit PC.dig as structural Verilog
module PC (
  input  [15:0] D_ISRAM,
  input  WE_ISRAM,
  input  [15:0] D_Page,
  input  [7:0] ADDR_ISRAM,
  input  WE_Page,
  input  WE_PC,
  input  [7:0] ADDR_PC,
  input  RST_PC,
  input  RST_Page,
  input  CLK,
  input  Disable_PC,
  input  AsencEnable_PC,
  output [15:0] Page_Num,
  output [15:0] IS_Out
);

  wire and_1_out, and_2_out, d_ff_1_q, jk_ff_1_q, jk_ff_2_q, not_1_out, or_1_out, or_2_out,
       Page_Counter_Page_ovf, Program_Counter_PC_ovf;
  wire [7:0] alu_regrst_1_q, or_3_out, Program_Counter_PC_out;
  wire [15:8] alu_regrst_1_q_2;

  not not_1 (not_1_out, Disable_PC);
  or or_1 (or_1_out, RST_Page, d_ff_1_q);
  CounterPreset #(.Bits(16)) Page_Counter_Page (
    .en(Program_Counter_PC_ovf), .C(CLK), .dir(1'b0), .in(D_Page), .ld(WE_Page), .clr(or_1_out),
    .out(Page_Num), .ovf(Page_Counter_Page_ovf));
  JK_FF jk_ff_1 (.J(1'b1), .C(CLK), .K(1'b1), .Q(jk_ff_1_q));  // open: nQ
  D_FF d_ff_1 (.D(Page_Counter_Page_ovf), .C(CLK), .Q(d_ff_1_q));  // open: nQ
  and and_1 (and_1_out, not_1_out, and_2_out);
  or or_2 (or_2_out, and_1_out, AsencEnable_PC);
  JK_FF jk_ff_2 (.J(jk_ff_1_q), .C(CLK), .K(jk_ff_1_q), .Q(jk_ff_2_q));  // open: nQ
  CounterPreset #(.Bits(8)) Program_Counter_PC (
    .en(or_2_out), .C(CLK), .dir(1'b0), .in(ADDR_PC), .ld(WE_PC), .clr(RST_PC), .out(Program_Counter_PC_out),
    .ovf(Program_Counter_PC_ovf));
  and and_2 (and_2_out, jk_ff_1_q, jk_ff_2_q);
  ALU_RegRST alu_regrst_1 (.D({{8{1'b0}}, ADDR_ISRAM}), .RST(not_1_out), .Q({alu_regrst_1_q_2, alu_regrst_1_q}));
  assign or_3_out = alu_regrst_1_q | Program_Counter_PC_out;  // Or or_3, 8 bits wide
  BlockRAMDualPort #(.AddrBits(8), .isProgramMemory("true"), .Bits(16)) Instraction_Memory (
    .A(or_3_out), .Din(D_ISRAM), .str(WE_ISRAM), .C(CLK), .D(IS_Out));

  // Notes on the sheet:
  //   D_ISRAM: Data input for instraction memory
  //   WE_ISRAM: Write enable input for instraction memory
  //   D_Page: Data input for Page Counter
  //   ADDR_ISRAM: Adress input for instraction memory
  //   WE_Page: Write Enable input for Page Counter
  //   WE_PC: Write enable input for Program Counter
  //   ADDR_PC: Adress input for Program Counter
  //   RST_PC: Reset input for Program Counter
  //   Disable_PC: Disable input for Program Counter
  //   Page_Num: Page Number out
  //   IS_Out: Instraction Output
  //   AsencEnable_PC: Disable input for Program Counter
endmodule
