// Digital circuit RegFile32Bayt.dig as structural Verilog
module RegFile32Bayt (
  input  D0,
  input  D1,
  input  D2,
  input  D3,
  input  D4,
  input  D5,
  input  D6,
  input  D7,
  input  D8,
  input  D9,
  input  D10,
  input  D11,
  input  D12,
  input  D13,
  input  D14,
  input  D15,
  input  SEL0_In,
  input  SEL1_In,
  input  SEL2_In,
  input  SEL3_In,
  input  SEL0_Out0,
  input  SEL1_Out0,
  input  SEL2_Out0,
  input  SEL3_Out0,
  input  SEL0_Out1,
  input  SEL1_Out1,
  input  SEL2_Out1,
  input  SEL3_Out1,
  input  CLK,
  input  EN_Write,
  output Q0_0,
  output Q0_1,
  output Q0_2,
  output Q0_3,
  output Q0_4,
  output Q0_5,
  output Q0_6,
  output Q0_7,
  output Q0_8,
  output Q0_9,
  output Q0_10,
  output Q0_11,
  output Q0_12,
  output Q0_13,
  output Q0_14,
  output Q0_15,
  output Q1_0,
  output Q1_1,
  output Q1_2,
  output Q1_3,
  output Q1_4,
  output Q1_5,
  output Q1_6,
  output Q1_7,
  output Q1_8,
  output Q1_9,
  output Q1_10,
  output Q1_11,
  output Q1_12,
  output Q1_13,
  output Q1_14,
  output Q1_15
);

  wire _16_bitmuxwithenablepin_1_q0, _16_bitmuxwithenablepin_1_q1, _16_bitmuxwithenablepin_1_q2,
       _16_bitmuxwithenablepin_1_q3, _16_bitmuxwithenablepin_1_q4, _16_bitmuxwithenablepin_1_q5,
       _16_bitmuxwithenablepin_1_q6, _16_bitmuxwithenablepin_1_q7, _16_bitmuxwithenablepin_1_q8,
       _16_bitmuxwithenablepin_1_q9, _16_bitmuxwithenablepin_1_q10, _16_bitmuxwithenablepin_1_q11,
       _16_bitmuxwithenablepin_1_q12, _16_bitmuxwithenablepin_1_q13, _16_bitmuxwithenablepin_1_q14,
       _16_bitmuxwithenablepin_1_q15;
  wire [15:0] undriven, undriven_2, undriven_3, undriven_4, undriven_5, undriven_6, undriven_7, undriven_8,
       undriven_9, undriven_10, undriven_11, undriven_12, undriven_13, undriven_14, undriven_15, undriven_16;

  _16_BitMuxWithEnablePin _16_bitmuxwithenablepin_1 (
    .EN(EN_Write), .Sel_4Bit({SEL3_In, SEL2_In, SEL1_In, SEL0_In}), .Q0(_16_bitmuxwithenablepin_1_q0),
    .Q1(_16_bitmuxwithenablepin_1_q1), .Q2(_16_bitmuxwithenablepin_1_q2), .Q3(_16_bitmuxwithenablepin_1_q3),
    .Q4(_16_bitmuxwithenablepin_1_q4), .Q5(_16_bitmuxwithenablepin_1_q5), .Q6(_16_bitmuxwithenablepin_1_q6),
    .Q7(_16_bitmuxwithenablepin_1_q7), .Q8(_16_bitmuxwithenablepin_1_q8), .Q9(_16_bitmuxwithenablepin_1_q9),
    .Q10(_16_bitmuxwithenablepin_1_q10), .Q11(_16_bitmuxwithenablepin_1_q11),
    .Q12(_16_bitmuxwithenablepin_1_q12), .Q13(_16_bitmuxwithenablepin_1_q13),
    .Q14(_16_bitmuxwithenablepin_1_q14), .Q15(_16_bitmuxwithenablepin_1_q15));
  // _16_BitRegister _16_bitregister_1: pin names not known; wires that end beside it: {D15, D14, D13, D12, D11, D10, D9, D8, D7, D6, D5, D4, D3, D2, D1, D0}, _16_bitmuxwithenablepin_1_q0, CLK
  // _16_BitRegister _16_bitregister_2: pin names not known; wires that end beside it: {D15, D14, D13, D12, D11, D10, D9, D8, D7, D6, D5, D4, D3, D2, D1, D0}, _16_bitmuxwithenablepin_1_q4, CLK
  // _16_BitRegister _16_bitregister_3: pin names not known; wires that end beside it: {D15, D14, D13, D12, D11, D10, D9, D8, D7, D6, D5, D4, D3, D2, D1, D0}, _16_bitmuxwithenablepin_1_q8, CLK
  // _16_BitRegister _16_bitregister_4: pin names not known; wires that end beside it: {D15, D14, D13, D12, D11, D10, D9, D8, D7, D6, D5, D4, D3, D2, D1, D0}, _16_bitmuxwithenablepin_1_q12, CLK
  // _16_BitRegister _16_bitregister_5: pin names not known; wires that end beside it: {D15, D14, D13, D12, D11, D10, D9, D8, D7, D6, D5, D4, D3, D2, D1, D0}, _16_bitmuxwithenablepin_1_q1, CLK
  // _16_BitRegister _16_bitregister_6: pin names not known; wires that end beside it: {D15, D14, D13, D12, D11, D10, D9, D8, D7, D6, D5, D4, D3, D2, D1, D0}, _16_bitmuxwithenablepin_1_q5, CLK
  // _16_BitRegister _16_bitregister_7: pin names not known; wires that end beside it: {D15, D14, D13, D12, D11, D10, D9, D8, D7, D6, D5, D4, D3, D2, D1, D0}, _16_bitmuxwithenablepin_1_q9, CLK
  // _16_BitRegister _16_bitregister_8: pin names not known; wires that end beside it: {D15, D14, D13, D12, D11, D10, D9, D8, D7, D6, D5, D4, D3, D2, D1, D0}, _16_bitmuxwithenablepin_1_q13, CLK
  // _16_BitRegister _16_bitregister_9: pin names not known; wires that end beside it: {D15, D14, D13, D12, D11, D10, D9, D8, D7, D6, D5, D4, D3, D2, D1, D0}, _16_bitmuxwithenablepin_1_q2, CLK
  // _16_BitRegister _16_bitregister_10: pin names not known; wires that end beside it: {D15, D14, D13, D12, D11, D10, D9, D8, D7, D6, D5, D4, D3, D2, D1, D0}, _16_bitmuxwithenablepin_1_q6, CLK
  // _16_BitRegister _16_bitregister_11: pin names not known; wires that end beside it: {D15, D14, D13, D12, D11, D10, D9, D8, D7, D6, D5, D4, D3, D2, D1, D0}, _16_bitmuxwithenablepin_1_q10, CLK
  // _16_BitRegister _16_bitregister_12: pin names not known; wires that end beside it: {D15, D14, D13, D12, D11, D10, D9, D8, D7, D6, D5, D4, D3, D2, D1, D0}, _16_bitmuxwithenablepin_1_q14, CLK
  // _16_BitRegister _16_bitregister_13: pin names not known; wires that end beside it: {D15, D14, D13, D12, D11, D10, D9, D8, D7, D6, D5, D4, D3, D2, D1, D0}, _16_bitmuxwithenablepin_1_q3, CLK
  // _16_BitRegister _16_bitregister_14: pin names not known; wires that end beside it: {D15, D14, D13, D12, D11, D10, D9, D8, D7, D6, D5, D4, D3, D2, D1, D0}, _16_bitmuxwithenablepin_1_q7, CLK
  // _16_BitRegister _16_bitregister_15: pin names not known; wires that end beside it: {D15, D14, D13, D12, D11, D10, D9, D8, D7, D6, D5, D4, D3, D2, D1, D0}, _16_bitmuxwithenablepin_1_q11, CLK
  // _16_BitRegister _16_bitregister_16: pin names not known; wires that end beside it: {D15, D14, D13, D12, D11, D10, D9, D8, D7, D6, D5, D4, D3, D2, D1, D0}, _16_bitmuxwithenablepin_1_q15, CLK
  Multiplexer #(.Bits(16), .Selector_Bits(4)) multiplexer_1 (
    .sel({SEL3_Out0, SEL2_Out0, SEL1_Out0, SEL0_Out0}), .in_0(undriven_16), .in_1(undriven_12),
    .in_2(undriven_2), .in_3(undriven_15), .in_4(undriven_10), .in_5(undriven_11), .in_6(undriven_13),
    .in_7(undriven_14), .in_8(undriven_9), .in_9(undriven_8), .in_10(undriven_3), .in_11(undriven_7),
    .in_12(undriven), .in_13(undriven_6), .in_14(undriven_4), .in_15(undriven_5),
    .out({Q0_15, Q0_14, Q0_13, Q0_12, Q0_11, Q0_10, Q0_9, Q0_8, Q0_7, Q0_6, Q0_5, Q0_4, Q0_3, Q0_2, Q0_1, Q0_0}));
  Multiplexer #(.Selector_Bits(4), .Bits(16)) multiplexer_2 (
    .sel({SEL3_Out1, SEL2_Out1, SEL1_Out1, SEL0_Out1}), .in_0(undriven_16), .in_1(undriven_12),
    .in_2(undriven_2), .in_3(undriven_15), .in_4(undriven_10), .in_5(undriven_11), .in_6(undriven_13),
    .in_7(undriven_14), .in_8(undriven_9), .in_9(undriven_8), .in_10(undriven_3), .in_11(undriven_7),
    .in_12(undriven), .in_13(undriven_6), .in_14(undriven_4), .in_15(undriven_5),
    .out({Q1_15, Q1_14, Q1_13, Q1_12, Q1_11, Q1_10, Q1_9, Q1_8, Q1_7, Q1_6, Q1_5, Q1_4, Q1_3, Q1_2, Q1_1, Q1_0}));
endmodule
