// Digital circuit RegisterFile.dig as structural Verilog
module RegisterFile (
  input  CLK,
  input  [15:0] D,
  input  [3:0] GPREG_InSEL,
  input  [3:0] GPREG_OutSEL,
  input  [3:0] IO_InSel,
  input  [3:0] IO_OutSel,
  input  [15:0] BRAM_ADDR,
  input  BRAM_WE,
  input  [3:0] SetMod_IO,
  input  GPIO_IN0x0,
  input  GPIO_IN0x1,
  input  GPIO_IN0x2,
  input  GPIO_IN0x3,
  input  GPIO_IN0x4,
  input  GPIO_IN0x5,
  input  GPIO_IN0x6,
  input  GPIO_IN0x7,
  input  GPIO_IN0x8,
  input  GPIO_IN0x9,
  input  GPIO_IN0xA,
  input  GPIO_IN0xB,
  input  GPIO_IN0xC,
  input  GPIO_IN0xD,
  input  GPIO_IN0xE,
  input  GPIO_IN0xF,
  output [15:0] GPREG_UOT,
  output GPIO_OUT0x0,
  output GPIO_DataOUT,
  output [15:0] BRAM_OUT,
  output GPIO_OUT0x1,
  output GPIO_OUT0x2,
  output GPIO_OUT0x3,
  output GPIO_OUT0x4,
  output GPIO_OUT0x5,
  output GPIO_OUT0x6,
  output GPIO_OUT0x7,
  output GPIO_OUT0x8,
  output GPIO_OUT0x9,
  output GPIO_OUT0xA,
  output GPIO_OUT0xB,
  output GPIO_OUT0xC,
  output GPIO_OUT0xD,
  output GPIO_OUT0xE,
  output GPIO_OUT0xF
);

  wire decoder_1_out_0, decoder_1_out_1, decoder_1_out_2, decoder_1_out_3, decoder_1_out_4, decoder_1_out_5,
       decoder_1_out_6, decoder_1_out_7, decoder_1_out_8, decoder_1_out_9, decoder_1_out_10,
       decoder_1_out_11, decoder_1_out_12, decoder_1_out_13, decoder_1_out_14, decoder_1_out_15,
       decoder_2_out_0, decoder_2_out_1, decoder_2_out_2, decoder_2_out_3, decoder_2_out_4, decoder_2_out_5,
       decoder_2_out_6, decoder_2_out_7, decoder_2_out_8, decoder_2_out_9, decoder_2_out_10,
       decoder_2_out_11, decoder_2_out_12, decoder_2_out_13, decoder_2_out_14, decoder_2_out_15,
       decoder_3_out_0, decoder_3_out_1, decoder_3_out_2, decoder_3_out_3, decoder_3_out_4, decoder_3_out_5,
       decoder_3_out_6, decoder_3_out_7, decoder_3_out_8, decoder_3_out_9, decoder_3_out_10,
       decoder_3_out_11, decoder_3_out_12, decoder_3_out_13, decoder_3_out_14, decoder_3_out_15,
       register_1_q, register_2_q, register_3_q, register_4_q, register_13_q, register_14_q, register_15_q,
       register_16_q, register_25_q, register_26_q, register_27_q, register_28_q, register_37_q,
       register_38_q, register_39_q, register_40_q;
  wire [7:0] or_8_out, or_12_out;
  wire [15:0] multiplexer_16_out, not_1_out, register_5_q, register_6_q, register_7_q, register_8_q,
       register_12_q, register_17_q, register_18_q, register_19_q, register_20_q, register_29_q,
       register_30_q, register_31_q, register_32_q, register_41_q, register_42_q, register_43_q,
       register_44_q;

  assign not_1_out = ~register_12_q;  // Not not_1, 16 bits wide
  Decoder #(.Selector_Bits(4)) decoder_1 (
    .sel(IO_InSel), .out_0(decoder_1_out_0), .out_1(decoder_1_out_1), .out_2(decoder_1_out_2),
    .out_3(decoder_1_out_3), .out_4(decoder_1_out_4), .out_5(decoder_1_out_5), .out_6(decoder_1_out_6),
    .out_7(decoder_1_out_7), .out_8(decoder_1_out_8), .out_9(decoder_1_out_9), .out_10(decoder_1_out_10),
    .out_11(decoder_1_out_11), .out_12(decoder_1_out_12), .out_13(decoder_1_out_13),
    .out_14(decoder_1_out_14), .out_15(decoder_1_out_15));
  or or_1 (or_8_out[0], decoder_1_out_0, register_12_q[0]);
  or or_2 (or_8_out[1], decoder_1_out_1, register_12_q[1]);
  or or_3 (or_8_out[2], decoder_1_out_2, register_12_q[2]);
  or or_4 (or_8_out[3], decoder_1_out_3, register_12_q[3]);
  or or_5 (or_8_out[4], decoder_1_out_4, register_12_q[4]);
  or or_6 (or_8_out[5], decoder_1_out_5, register_12_q[5]);
  or or_7 (or_8_out[6], decoder_1_out_6, register_12_q[6]);
  or or_8 (or_8_out[7], decoder_1_out_7, register_12_q[7]);
  Multiplexer multiplexer_1 (.sel(not_1_out[0]), .in_0(D[0]), .in_1(GPIO_IN0x0), .out(multiplexer_16_out[0]));
  Multiplexer multiplexer_2 (.sel(not_1_out[1]), .in_0(D[1]), .in_1(GPIO_IN0x1), .out(multiplexer_16_out[1]));
  Multiplexer multiplexer_3 (.sel(not_1_out[2]), .in_0(D[2]), .in_1(GPIO_IN0x2), .out(multiplexer_16_out[2]));
  Multiplexer multiplexer_4 (.sel(not_1_out[3]), .in_0(D[3]), .in_1(GPIO_IN0x3), .out(multiplexer_16_out[3]));
  Multiplexer multiplexer_5 (.sel(not_1_out[4]), .in_0(D[4]), .in_1(GPIO_IN0x4), .out(multiplexer_16_out[4]));
  Multiplexer multiplexer_6 (.sel(not_1_out[5]), .in_0(D[5]), .in_1(GPIO_IN0x5), .out(multiplexer_16_out[5]));
  Multiplexer multiplexer_7 (.sel(not_1_out[6]), .in_0(D[6]), .in_1(GPIO_IN0x6), .out(multiplexer_16_out[6]));
  Multiplexer multiplexer_8 (.sel(not_1_out[7]), .in_0(D[7]), .in_1(GPIO_IN0x7), .out(multiplexer_16_out[7]));
  Multiplexer multiplexer_9 (.sel(not_1_out[8]), .in_0(D[8]), .in_1(GPIO_IN0x8), .out(multiplexer_16_out[8]));
  Multiplexer multiplexer_10 (.sel(not_1_out[9]), .in_0(D[9]), .in_1(GPIO_IN0x9), .out(multiplexer_16_out[9]));
  Multiplexer multiplexer_11 (.sel(not_1_out[10]), .in_0(D[10]), .in_1(GPIO_IN0xA), .out(multiplexer_16_out[10]));
  Multiplexer multiplexer_12 (.sel(not_1_out[11]), .in_0(D[11]), .in_1(GPIO_IN0xB), .out(multiplexer_16_out[11]));
  Multiplexer multiplexer_13 (.sel(not_1_out[12]), .in_0(D[12]), .in_1(GPIO_IN0xC), .out(multiplexer_16_out[12]));
  Multiplexer multiplexer_14 (.sel(not_1_out[13]), .in_0(D[13]), .in_1(GPIO_IN0xD), .out(multiplexer_16_out[13]));
  Multiplexer multiplexer_15 (.sel(not_1_out[14]), .in_0(D[14]), .in_1(GPIO_IN0xE), .out(multiplexer_16_out[14]));
  Multiplexer multiplexer_16 (.sel(not_1_out[15]), .in_0(D[15]), .in_1(GPIO_IN0xF), .out(multiplexer_16_out[15]));
  or or_9 (or_12_out[0], decoder_1_out_8, register_12_q[8]);
  or or_10 (or_12_out[1], decoder_1_out_9, register_12_q[9]);
  or or_11 (or_12_out[2], decoder_1_out_10, register_12_q[10]);
  or or_12 (or_12_out[3], decoder_1_out_11, register_12_q[11]);
  or or_13 (or_12_out[4], decoder_1_out_12, register_12_q[12]);
  or or_14 (or_12_out[5], decoder_1_out_13, register_12_q[13]);
  or or_15 (or_12_out[6], decoder_1_out_14, register_12_q[14]);
  or or_16 (or_12_out[7], decoder_1_out_15, register_12_q[15]);
  Decoder #(.Selector_Bits(4)) decoder_2 (
    .sel(GPREG_InSEL), .out_0(decoder_2_out_0), .out_1(decoder_2_out_1), .out_2(decoder_2_out_2),
    .out_3(decoder_2_out_3), .out_4(decoder_2_out_4), .out_5(decoder_2_out_5), .out_6(decoder_2_out_6),
    .out_7(decoder_2_out_7), .out_8(decoder_2_out_8), .out_9(decoder_2_out_9), .out_10(decoder_2_out_10),
    .out_11(decoder_2_out_11), .out_12(decoder_2_out_12), .out_13(decoder_2_out_13),
    .out_14(decoder_2_out_14), .out_15(decoder_2_out_15));
  Decoder #(.Selector_Bits(4)) decoder_3 (
    .sel(SetMod_IO), .out_0(decoder_3_out_0), .out_1(decoder_3_out_1), .out_2(decoder_3_out_2),
    .out_3(decoder_3_out_3), .out_4(decoder_3_out_4), .out_5(decoder_3_out_5), .out_6(decoder_3_out_6),
    .out_7(decoder_3_out_7), .out_8(decoder_3_out_8), .out_9(decoder_3_out_9), .out_10(decoder_3_out_10),
    .out_11(decoder_3_out_11), .out_12(decoder_3_out_12), .out_13(decoder_3_out_13),
    .out_14(decoder_3_out_14), .out_15(decoder_3_out_15));
  Register register_1 (.D(multiplexer_16_out[12]), .C(CLK), .en(or_8_out[0]), .Q(register_1_q));
  Register register_2 (.D(multiplexer_16_out[13]), .C(CLK), .en(or_8_out[1]), .Q(register_2_q));
  Register register_3 (.D(multiplexer_16_out[14]), .C(CLK), .en(or_8_out[2]), .Q(register_3_q));
  Register register_4 (.D(multiplexer_16_out[15]), .C(CLK), .en(or_8_out[3]), .Q(register_4_q));
  Register #(.Bits(16)) register_5 (.D(D), .C(CLK), .en(decoder_2_out_0), .Q(register_5_q));
  Register #(.Bits(16)) register_6 (.D(D), .C(CLK), .en(decoder_2_out_1), .Q(register_6_q));
  Register #(.Bits(16)) register_7 (.D(D), .C(CLK), .en(decoder_2_out_2), .Q(register_7_q));
  Register #(.Bits(16)) register_8 (.D(D), .C(CLK), .en(decoder_2_out_3), .Q(register_8_q));
  BlockRAMDualPort #(.AddrBits(16), .Bits(16)) blockramdualport_1 (
    .A(BRAM_ADDR), .Din(D), .str(BRAM_WE), .C(CLK), .D(BRAM_OUT));
  Register register_9 (.D(D[0]), .C(CLK), .en(decoder_3_out_0), .Q(register_12_q[0]));
  Register register_10 (.D(D[0]), .C(CLK), .en(decoder_3_out_1), .Q(register_12_q[1]));
  Register register_11 (.D(D[0]), .C(CLK), .en(decoder_3_out_2), .Q(register_12_q[2]));
  Register register_12 (.D(D[0]), .C(CLK), .en(decoder_3_out_3), .Q(register_12_q[3]));
  and and_1 (GPIO_OUT0x0, register_1_q, register_12_q[0]);
  and and_2 (GPIO_OUT0x1, register_2_q, register_12_q[1]);
  and and_3 (GPIO_OUT0x2, register_3_q, register_12_q[2]);
  and and_4 (GPIO_OUT0x3, register_4_q, register_12_q[3]);
  Register register_13 (.D(multiplexer_16_out[8]), .C(CLK), .en(or_8_out[4]), .Q(register_13_q));
  Register register_14 (.D(multiplexer_16_out[9]), .C(CLK), .en(or_8_out[5]), .Q(register_14_q));
  Register register_15 (.D(multiplexer_16_out[10]), .C(CLK), .en(or_8_out[6]), .Q(register_15_q));
  Register register_16 (.D(multiplexer_16_out[11]), .C(CLK), .en(or_8_out[7]), .Q(register_16_q));
  Register #(.Bits(16)) register_17 (.D(D), .C(CLK), .en(decoder_2_out_4), .Q(register_17_q));
  Register #(.Bits(16)) register_18 (.D(D), .C(CLK), .en(decoder_2_out_5), .Q(register_18_q));
  Register #(.Bits(16)) register_19 (.D(D), .C(CLK), .en(decoder_2_out_6), .Q(register_19_q));
  Register #(.Bits(16)) register_20 (.D(D), .C(CLK), .en(decoder_2_out_7), .Q(register_20_q));
  and and_5 (GPIO_OUT0x4, register_13_q, register_12_q[4]);
  and and_6 (GPIO_OUT0x5, register_14_q, register_12_q[5]);
  and and_7 (GPIO_OUT0x6, register_15_q, register_12_q[6]);
  and and_8 (GPIO_OUT0x7, register_16_q, register_12_q[7]);
  Register register_21 (.D(D[0]), .C(CLK), .en(decoder_3_out_4), .Q(register_12_q[4]));
  Register register_22 (.D(D[0]), .C(CLK), .en(decoder_3_out_5), .Q(register_12_q[5]));
  Register register_23 (.D(D[0]), .C(CLK), .en(decoder_3_out_6), .Q(register_12_q[6]));
  Register register_24 (.D(D[0]), .C(CLK), .en(decoder_3_out_7), .Q(register_12_q[7]));
  Register register_25 (.D(multiplexer_16_out[4]), .C(CLK), .en(or_12_out[0]), .Q(register_25_q));
  Register register_26 (.D(multiplexer_16_out[5]), .C(CLK), .en(or_12_out[1]), .Q(register_26_q));
  Register register_27 (.D(multiplexer_16_out[6]), .C(CLK), .en(or_12_out[2]), .Q(register_27_q));
  Register register_28 (.D(multiplexer_16_out[7]), .C(CLK), .en(or_12_out[3]), .Q(register_28_q));
  Register #(.Bits(16)) register_29 (.D(D), .C(CLK), .en(decoder_2_out_8), .Q(register_29_q));
  Register #(.Bits(16)) register_30 (.D(D), .C(CLK), .en(decoder_2_out_9), .Q(register_30_q));
  Register #(.Bits(16)) register_31 (.D(D), .C(CLK), .en(decoder_2_out_10), .Q(register_31_q));
  Register #(.Bits(16)) register_32 (.D(D), .C(CLK), .en(decoder_2_out_11), .Q(register_32_q));
  and and_9 (GPIO_OUT0x8, register_25_q, register_12_q[8]);
  and and_10 (GPIO_OUT0x9, register_26_q, register_12_q[9]);
  and and_11 (GPIO_OUT0xA, register_27_q, register_12_q[10]);
  and and_12 (GPIO_OUT0xB, register_28_q, register_12_q[11]);
  Register register_33 (.D(D[0]), .C(CLK), .en(decoder_3_out_8), .Q(register_12_q[8]));
  Register register_34 (.D(D[0]), .C(CLK), .en(decoder_3_out_9), .Q(register_12_q[9]));
  Register register_35 (.D(D[0]), .C(CLK), .en(decoder_3_out_10), .Q(register_12_q[10]));
  Register register_36 (.D(D[0]), .C(CLK), .en(decoder_3_out_11), .Q(register_12_q[11]));
  Register register_37 (.D(multiplexer_16_out[0]), .C(CLK), .en(or_12_out[4]), .Q(register_37_q));
  Register register_38 (.D(multiplexer_16_out[1]), .C(CLK), .en(or_12_out[5]), .Q(register_38_q));
  Register register_39 (.D(multiplexer_16_out[2]), .C(CLK), .en(or_12_out[6]), .Q(register_39_q));
  Register register_40 (.D(multiplexer_16_out[3]), .C(CLK), .en(or_12_out[7]), .Q(register_40_q));
  Register #(.Bits(16)) register_41 (.D(D), .C(CLK), .en(decoder_2_out_12), .Q(register_41_q));
  Register #(.Bits(16)) register_42 (.D(D), .C(CLK), .en(decoder_2_out_13), .Q(register_42_q));
  Register #(.Bits(16)) register_43 (.D(D), .C(CLK), .en(decoder_2_out_14), .Q(register_43_q));
  Register #(.Bits(16)) register_44 (.D(D), .C(CLK), .en(decoder_2_out_15), .Q(register_44_q));
  Register register_45 (.D(D[0]), .C(CLK), .en(decoder_3_out_12), .Q(register_12_q[12]));
  Register register_46 (.D(D[0]), .C(CLK), .en(decoder_3_out_13), .Q(register_12_q[13]));
  Register register_47 (.D(D[0]), .C(CLK), .en(decoder_3_out_14), .Q(register_12_q[14]));
  Register register_48 (.D(D[0]), .C(CLK), .en(decoder_3_out_15), .Q(register_12_q[15]));
  and and_13 (GPIO_OUT0xC, register_37_q, register_12_q[12]);
  and and_14 (GPIO_OUT0xD, register_38_q, register_12_q[13]);
  and and_15 (GPIO_OUT0xE, register_39_q, register_12_q[14]);
  and and_16 (GPIO_OUT0xF, register_40_q, register_12_q[15]);
  Multiplexer #(.Selector_Bits(4)) multiplexer_17 (
    .sel(IO_OutSel), .in_0(register_1_q), .in_1(register_2_q), .in_2(register_3_q), .in_3(register_4_q),
    .in_4(register_13_q), .in_5(register_14_q), .in_6(register_15_q), .in_7(register_16_q),
    .in_8(register_25_q), .in_9(register_26_q), .in_10(register_27_q), .in_11(register_28_q),
    .in_12(register_37_q), .in_13(register_38_q), .in_14(register_39_q), .in_15(register_40_q),
    .out(GPIO_DataOUT));
  Multiplexer #(.Selector_Bits(4), .Bits(16)) multiplexer_18 (
    .sel(GPREG_OutSEL), .in_0(register_5_q), .in_1(register_6_q), .in_2(register_7_q), .in_3(register_8_q),
    .in_4(register_17_q), .in_5(register_18_q), .in_6(register_19_q), .in_7(register_20_q),
    .in_8(register_29_q), .in_9(register_30_q), .in_10(register_31_q), .in_11(register_32_q),
    .in_12(register_41_q), .in_13(register_42_q), .in_14(register_43_q), .in_15(register_44_q),
    .out(GPREG_UOT));
endmodule
