// Digital circuit gpio_cell.dig as structural Verilog
module gpio_cell (
  input  REG_WR,
  input  OE,
  input  CLK,
  input  WE,
  output REG_RD,
  output PIN_OUT
);

  wire and_1_out, register_1_q;

  buf and_1 (and_1_out, REG_WR);  // And open: In_1
  Register register_1 (.D(and_1_out), .C(CLK), .en(WE), .Q(register_1_q));
  // PinControl pincontrol_1: pin names not known; wires that end beside it: register_1_q, OE, REG_RD, PIN_OUT
endmodule
