// Digital circuit lsu.dig as structural Verilog
module lsu (
  input  LSU_EN,
  input  [3:0] LSU_OP,
  input  CLK,
  input  [3:0] SOURCE,
  input  [3:0] TARGET,
  input  [15:0] DATA,
  output [15:0] Register_DataOut,
  output [15:0] Memory_DataOut,
  output [15:0] GPIO_REG_DataOut,
  output [15:0] PC_DataOut,
  output [3:0] SOURCE_MEM,
  output [3:0] SOURCE_REG,
  output [3:0] SOURCE_IM,
  output [3:0] SOURCE_GPIO,
  output [3:0] TARGET_REG,
  output [3:0] TARGET_MEM,
  output [3:0] TARGET_GPIO,
  output [3:0] TARGET_PC,
  output Restore_PC,
  output SOURCE_FUNCREG,
  output PC_NPS
);

  wire _16_bitdecoderwithenablepin_1_q0, _16_bitdecoderwithenablepin_1_q1, _16_bitdecoderwithenablepin_1_q2,
       _16_bitdecoderwithenablepin_1_q3, _16_bitdecoderwithenablepin_1_q4, _16_bitdecoderwithenablepin_1_q5,
       _16_bitdecoderwithenablepin_1_q6, _16_bitdecoderwithenablepin_1_q7, _16_bitdecoderwithenablepin_1_q8,
       _16_bitdecoderwithenablepin_1_q9, _16_bitdecoderwithenablepin_1_q10,
       _16_bitdecoderwithenablepin_1_q11, _16_bitdecoderwithenablepin_1_q12,
       _16_bitdecoderwithenablepin_1_q13, _16_bitdecoderwithenablepin_1_q14,
       _16_bitdecoderwithenablepin_1_q15, alu_regctrl_1_q_1, alu_regctrl_1_q_2, alu_regctrl_1_q_3,
       alu_regctrl_1_q_4, alu_regctrl_1_q_5, alu_regctrl_1_q_6, alu_regctrl_1_q_7, alu_regctrl_1_q_8,
       alu_regctrl_1_q_9, alu_regctrl_1_q_a, alu_regctrl_1_q_b, alu_regctrl_1_q_c, alu_regctrl_1_q_d,
       alu_regctrl_1_q_e, alu_regctrl_1_q_f, alu_regctrl_1_rst, and_1_out, nand_1_out, nand_2_out,
       nand_3_out, not_1_out, or_4_out, or_7_out;
  wire [3:0] alu_regctrl_1_opcode_out, demultiplexer_1_out_1, demultiplexer_1_out_2, demultiplexer_1_out_3,
       demultiplexer_1_out_4, demultiplexer_1_out_5, demultiplexer_1_out_6, demultiplexer_1_out_7,
       demultiplexer_1_out_8, demultiplexer_1_out_9, demultiplexer_1_out_10, demultiplexer_1_out_11,
       demultiplexer_1_out_12, demultiplexer_1_out_13, demultiplexer_1_out_14, demultiplexer_1_out_15,
       demultiplexer_2_out_1, demultiplexer_2_out_2, demultiplexer_2_out_3, demultiplexer_2_out_4,
       demultiplexer_2_out_5, demultiplexer_2_out_7, demultiplexer_2_out_8, demultiplexer_2_out_9,
       demultiplexer_2_out_10, demultiplexer_2_out_11, demultiplexer_2_out_12, demultiplexer_2_out_13,
       demultiplexer_2_out_14, register_1_q, register_2_q;
  wire [3:1] demultiplexer_2_out_15;
  wire [7:0] register_4_q;
  wire [15:0] add_1_s, alu_regrst_1_q, alu_regrst_2_q, alu_regrst_3_q, alu_regrst_4_q, demultiplexer_3_out_1,
       demultiplexer_3_out_2, demultiplexer_3_out_3, demultiplexer_3_out_4, demultiplexer_3_out_5,
       demultiplexer_3_out_6, demultiplexer_3_out_7, demultiplexer_3_out_8, demultiplexer_3_out_9,
       demultiplexer_3_out_10, demultiplexer_3_out_11, demultiplexer_3_out_12, demultiplexer_3_out_13,
       demultiplexer_3_out_14, demultiplexer_3_out_15, or_9_out, register_3_q, register_5_q;

  Register #(.Bits(4)) register_1 (.D(SOURCE), .C(CLK), .en(LSU_EN), .Q(register_1_q));
  Register #(.Bits(4)) register_2 (.D(TARGET), .C(CLK), .en(LSU_EN), .Q(register_2_q));
  _16_BitDecoderWithEnablePin _16_bitdecoderwithenablepin_1 (
    .EN(LSU_EN), .Sel_4Bit(LSU_OP), .Q0(_16_bitdecoderwithenablepin_1_q0),
    .Q1(_16_bitdecoderwithenablepin_1_q1), .Q2(_16_bitdecoderwithenablepin_1_q2),
    .Q3(_16_bitdecoderwithenablepin_1_q3), .Q4(_16_bitdecoderwithenablepin_1_q4),
    .Q5(_16_bitdecoderwithenablepin_1_q5), .Q6(_16_bitdecoderwithenablepin_1_q6),
    .Q7(_16_bitdecoderwithenablepin_1_q7), .Q8(_16_bitdecoderwithenablepin_1_q8),
    .Q9(_16_bitdecoderwithenablepin_1_q9), .Q10(_16_bitdecoderwithenablepin_1_q10),
    .Q11(_16_bitdecoderwithenablepin_1_q11), .Q12(_16_bitdecoderwithenablepin_1_q12),
    .Q13(_16_bitdecoderwithenablepin_1_q13), .Q14(_16_bitdecoderwithenablepin_1_q14),
    .Q15(_16_bitdecoderwithenablepin_1_q15));
  ALU_RegCtrl alu_regctrl_1 (
    .IsEn__Decoder(LSU_EN), .CLK(CLK), ._0x0(_16_bitdecoderwithenablepin_1_q0),
    ._0x1(_16_bitdecoderwithenablepin_1_q1), ._0x2(_16_bitdecoderwithenablepin_1_q2),
    ._0x3(_16_bitdecoderwithenablepin_1_q3), ._0x4(_16_bitdecoderwithenablepin_1_q4),
    ._0x5(_16_bitdecoderwithenablepin_1_q5), ._0x6(_16_bitdecoderwithenablepin_1_q6),
    ._0x7(_16_bitdecoderwithenablepin_1_q7), ._0x8(_16_bitdecoderwithenablepin_1_q8),
    ._0x9(_16_bitdecoderwithenablepin_1_q9), ._0xA(_16_bitdecoderwithenablepin_1_q10),
    ._0xB(_16_bitdecoderwithenablepin_1_q11), ._0xC(_16_bitdecoderwithenablepin_1_q12),
    ._0xD(_16_bitdecoderwithenablepin_1_q13), ._0xE(_16_bitdecoderwithenablepin_1_q14),
    ._0xF(_16_bitdecoderwithenablepin_1_q15), .OPCODE_IN(LSU_OP), .Q_1(alu_regctrl_1_q_1),
    .Q_2(alu_regctrl_1_q_2), .Q_3(alu_regctrl_1_q_3), .Q_4(alu_regctrl_1_q_4), .Q_5(alu_regctrl_1_q_5),
    .Q_6(alu_regctrl_1_q_6), .Q_7(alu_regctrl_1_q_7), .Q_8(alu_regctrl_1_q_8), .Q_9(alu_regctrl_1_q_9),
    .Q_A(alu_regctrl_1_q_a), .Q_B(alu_regctrl_1_q_b), .Q_C(alu_regctrl_1_q_c), .Q_D(alu_regctrl_1_q_d),
    .Q_E(alu_regctrl_1_q_e), .Q_F(alu_regctrl_1_q_f), .RST(alu_regctrl_1_rst),
    .OPCODE_OUT(alu_regctrl_1_opcode_out));  // open: Q_0
  not not_1 (not_1_out, alu_regctrl_1_rst);
  Demultiplexer #(.Selector_Bits(4), .Bits(4)) demultiplexer_1 (
    .sel(alu_regctrl_1_opcode_out), .in(register_2_q), .out_1(demultiplexer_1_out_1),
    .out_2(demultiplexer_1_out_2), .out_3(demultiplexer_1_out_3), .out_4(demultiplexer_1_out_4),
    .out_5(demultiplexer_1_out_5), .out_6(demultiplexer_1_out_6), .out_7(demultiplexer_1_out_7),
    .out_8(demultiplexer_1_out_8), .out_9(demultiplexer_1_out_9), .out_10(demultiplexer_1_out_10),
    .out_11(demultiplexer_1_out_11), .out_12(demultiplexer_1_out_12), .out_13(demultiplexer_1_out_13),
    .out_14(demultiplexer_1_out_14), .out_15(demultiplexer_1_out_15));  // open: out_0
  Demultiplexer #(.Selector_Bits(4), .Bits(4)) demultiplexer_2 (
    .sel(alu_regctrl_1_opcode_out), .in(register_1_q), .out_1(demultiplexer_2_out_1),
    .out_2(demultiplexer_2_out_2), .out_3(demultiplexer_2_out_3), .out_4(demultiplexer_2_out_4),
    .out_5(demultiplexer_2_out_5), .out_6(SOURCE_GPIO), .out_7(demultiplexer_2_out_7),
    .out_8(demultiplexer_2_out_8), .out_9(demultiplexer_2_out_9), .out_10(demultiplexer_2_out_10),
    .out_11(demultiplexer_2_out_11), .out_12(demultiplexer_2_out_12), .out_13(demultiplexer_2_out_13),
    .out_14(demultiplexer_2_out_14), .out_15({demultiplexer_2_out_15, SOURCE_FUNCREG}));  // open: out_0
  and and_1 (and_1_out, not_1_out, alu_regctrl_1_q_f);
  ALU_RegRST alu_regrst_1 (.D(DATA), .RST(alu_regctrl_1_rst), .Q(alu_regrst_1_q));
  D_FF d_ff_1 (.D(and_1_out), .C(CLK), .Q(Restore_PC));  // open: nQ
  assign TARGET_REG = demultiplexer_1_out_1 | demultiplexer_1_out_2 | demultiplexer_1_out_6 | demultiplexer_1_out_8 | demultiplexer_1_out_9;  // Or or_1, 4 bits wide
  assign SOURCE_MEM = demultiplexer_2_out_1 | demultiplexer_2_out_2;  // Or or_2, 4 bits wide
  assign SOURCE_REG = demultiplexer_2_out_3 | demultiplexer_2_out_4 | demultiplexer_2_out_5 | demultiplexer_2_out_8 | demultiplexer_2_out_11 | demultiplexer_2_out_13;  // Or or_3, 4 bits wide
  or or_4 (or_4_out, alu_regctrl_1_q_e, alu_regctrl_1_q_c, alu_regctrl_1_q_a, alu_regctrl_1_q_9, alu_regctrl_1_q_d, alu_regctrl_1_q_b, alu_regctrl_1_q_2, alu_regctrl_1_q_4, alu_regctrl_1_q_5, alu_regctrl_1_q_6, alu_regctrl_1_q_7, alu_regctrl_1_q_8);
  assign TARGET_MEM = demultiplexer_1_out_3 | demultiplexer_1_out_4 | demultiplexer_1_out_10;  // Or or_5, 4 bits wide
  assign SOURCE_IM = demultiplexer_2_out_9 | demultiplexer_2_out_7 | demultiplexer_2_out_10 | demultiplexer_2_out_12 | demultiplexer_2_out_14;  // Or or_6, 4 bits wide
  or or_7 (or_7_out, alu_regctrl_1_q_3, alu_regctrl_1_q_1);
  Add #(.Bits(16)) add_1 (.a(alu_regrst_1_q), .b(16'h1), .c_i(1'b0), .s(add_1_s), .c_o(PC_NPS));
  Register #(.Bits(16)) register_3 (.D(alu_regrst_1_q), .C(CLK), .en(or_4_out), .Q(register_3_q));
  Register #(.Bits(8)) register_4 (.D(alu_regrst_1_q[7:0]), .C(CLK), .en(or_7_out), .Q(register_4_q));
  Register #(.Bits(16)) register_5 (.D(add_1_s), .C(CLK), .en(alu_regctrl_1_q_f), .Q(register_5_q));
  nand nand_1 (nand_1_out, or_4_out, alu_regctrl_1_rst);
  nand nand_2 (nand_2_out, alu_regctrl_1_q_f, alu_regctrl_1_rst);
  assign TARGET_GPIO = demultiplexer_1_out_5 | demultiplexer_1_out_7;  // Or or_8, 4 bits wide
  ALU_RegRST alu_regrst_2 (.D(register_3_q), .RST(nand_1_out), .Q(alu_regrst_2_q));
  nand nand_3 (nand_3_out, alu_regctrl_1_rst, or_7_out);
  ALU_RegRST alu_regrst_3 (.D({{8{1'b0}}, register_4_q}), .RST(nand_3_out), .Q(alu_regrst_3_q));
  ALU_RegRST alu_regrst_4 (.D(register_5_q), .RST(nand_2_out), .Q(alu_regrst_4_q));
  assign or_9_out = alu_regrst_2_q | alu_regrst_3_q | alu_regrst_4_q;  // Or or_9, 16 bits wide
  Demultiplexer #(.Selector_Bits(4), .Bits(16)) demultiplexer_3 (
    .sel(alu_regctrl_1_opcode_out), .in(or_9_out), .out_1(demultiplexer_3_out_1),
    .out_2(demultiplexer_3_out_2), .out_3(demultiplexer_3_out_3), .out_4(demultiplexer_3_out_4),
    .out_5(demultiplexer_3_out_5), .out_6(demultiplexer_3_out_6), .out_7(demultiplexer_3_out_7),
    .out_8(demultiplexer_3_out_8), .out_9(demultiplexer_3_out_9), .out_10(demultiplexer_3_out_10),
    .out_11(demultiplexer_3_out_11), .out_12(demultiplexer_3_out_12), .out_13(demultiplexer_3_out_13),
    .out_14(demultiplexer_3_out_14), .out_15(demultiplexer_3_out_15));  // open: out_0
  assign TARGET_PC = demultiplexer_1_out_11 | demultiplexer_1_out_12 | demultiplexer_1_out_13 | demultiplexer_1_out_14 | demultiplexer_1_out_15;  // Or or_10, 4 bits wide
  assign Register_DataOut = demultiplexer_3_out_1 | demultiplexer_3_out_2 | demultiplexer_3_out_6 | demultiplexer_3_out_8 | demultiplexer_3_out_9;  // Or or_11, 16 bits wide
  assign Memory_DataOut = demultiplexer_3_out_3 | demultiplexer_3_out_4 | demultiplexer_3_out_10;  // Or or_12, 16 bits wide
  assign GPIO_REG_DataOut = demultiplexer_3_out_5 | demultiplexer_3_out_7;  // Or or_13, 16 bits wide
  assign PC_DataOut = demultiplexer_3_out_11 | demultiplexer_3_out_12 | demultiplexer_3_out_13 | demultiplexer_3_out_14 | demultiplexer_3_out_15;  // Or or_14, 16 bits wide

  // Notes on the sheet:
  //   DATA: This pipeline get data from source register
  //   PC_NPS: SEND NPS(NEXT PAGE SIGNAL) TO PC
endmodule
